# Fritzing sketch MorseBeacon (saved by Fritzing 0.8.5b)

parts:
  Composants1 = Arduino Uno (Rev3)
  Morse_Buzzer = Piezo Speaker
  R1 = Resistor [tolerance=±5% resistance=100 package="0603 [SMD]"]
  R2 = Resistor [tolerance=±5% resistance=1k package="0603 [SMD]"]
  Morse_LED = LED - 5mm [color="Red (633nm)" package="5 mm [THT]"]
  K2=Comm_K1=Morse = 2-Channel 5v Relay Shield [package=relay-2ch5v10a]
  Morse_Tone = POT_SWITCH [package=pot_pth_switch]
  Morse_Speed = POT_SWITCH [package=pot_pth_switch]
  Configuration_Switch = SPST Switch [package=switche-dpdt]

nets:
  N1: Composants1.A0, Morse_Speed.G$2_1
  N2: Composants1.A1, Morse_Tone.G$2_1
  N3: Composants1.D8, R1.Pin_1
  N4: Composants1.D11_PWM/MOSI, R2.Pin_1, K2=Comm_K1=Morse.IN2
  N5: Composants1.D12/MISO, K2=Comm_K1=Morse.IN1
  GND: Composants1.GND, Morse_Buzzer.pin1, Morse_LED.cathode, K2=Comm_K1=Morse.GND, Morse_Tone.G$2_2, Morse_Speed.G$2_2, Configuration_Switch.O
  N6: Composants1.D2, Configuration_Switch.P
  5V: Composants1.5V, K2=Comm_K1=Morse.VCC, Morse_Tone.G$1_A, Morse_Speed.G$1_A
  N7: Morse_Buzzer.pin2, R1.Pin_0
  N8: R2.Pin_0, Morse_LED.anode

custom parts:
  2-Channel 5v Relay Shield: 2 Channel 5v Relay Shield w. 2x SPD-06VDC-SD-C
